# Fritzing sketch potentiometer (saved by Fritzing 0.9.3b)

parts:
  Componente1 = Arduino Micro (Rev3)
  U1 = POT [package=alps_pot]

nets:
  N1: Componente1.GND, U1.E
  N2: Componente1.5V, U1.A
  N3: Componente1.A0, U1.S
